# Fritzing sketch mailbox_HELTEC_AB01_v1 (saved by Fritzing 0.9.4)

parts:
  S3 = SWITCH-MOMENTARY-2 [package=reed_switch_pth]
  S4 = SWITCH-MOMENTARY-2 [package=reed_switch_pth]
  Composant6 = Solar Cell
  BAT1 = 18650 battery holder [package=battery-18650-kit]  # not connected
  D1 = Schottky Diode [part_number=1N5817 package="300 mil [THT]"]
  Heltec_CubeCell_Dev-Board1 = Heltec CubeCell Dev-Board [part_number=HTCC-AB01]

nets:
  N1: S3.1, Composant6.-, Heltec_CubeCell_Dev-Board1.pin_11, Heltec_CubeCell_Dev-Board1.pin_14, Heltec_CubeCell_Dev-Board1.pin_18
  N2: S4.2, Heltec_CubeCell_Dev-Board1.pin3
  N3: Composant6.+, D1.anode
  N4: D1.cathode, Heltec_CubeCell_Dev-Board1.pin_15

notes:
  100 Ohms
  Light Contrast
  Motor
  Wake Up Manual
  LoRaWan Mailbox Notifier - HELTEC AB01 DEVKIT
  10 KOhms
  HELTEC AB01 DevKit
  vincent.huynen@gmail.com - December 2021 - Version 1
  NC
  NC : Normally Closed
  Flip Door - GPIO 1 / Pull-Up
  Flip Door
  Great Door - GPIO 2 / Pull-Up
  Built-in BMS (Battery Management System)
  Solar Panel - 5.5~7V
  Battery directly connected to SHT 1.25 on the back of the board

custom parts:
  18650 battery holder: 18650 Battery Holder
  Heltec CubeCell Dev-Board: CubeCell is a part of the Heltec LoRa series and incorporates an ASR6501 processor and SX1262 RF transceiver with an integrated CP2102 USB to serial port interface and onboard SHT1.25 battery interface with integrated lithium battery management system supporting direct solar panel connection.
